# Fritzing sketch google84 (saved by Fritzing 0.9.3b)
perfboards: 1

parts:
  U3 = ATTINY45 [package=dip]
  U4 = ESP8266 WiFi Module [part_number=ESP8266]

nets:
  N1: U3.GND, U4.REST
  N2: U3.PB0(MOSI), U4.VCC
  N3: U3.PB1(MISO), U4.GPIO_13
  N4: U3.VCC, U4.GPIO_2, U4.TXD
